# Fritzing sketch LM35 (saved by Fritzing 0.8.0b)
breadboards: 1

parts:
  Parte1 = Arduino Uno (Rev3)
  T1 = LM35 Temperature Sensor [package="TO92 [THT]"]

nets:
  N1: Parte1.A0, T1.Vout
  GND: Parte1.GND, T1.GND
  N2: Parte1.5V, T1.+Vs
