# Fritzing sketch Estor_PCB (saved by Fritzing 0.9.4)
circuit board: 8.46667cm x 5.64444cm
perfboards: 1

parts:
  NodeMCU = ESP8266 NodeMCU LoLin module
  M1 = Stepper Motor - Bipolar
  LED1 = LED - 5mm [color="Red (633nm)" package="5 mm [THT]"]
  LED0 = LED - 5mm [color="Red (633nm)" package="5 mm [THT]"]
  R1 = Resistor [tolerance=±5% resistance=220 package=THT]
  R2 = Resistor [tolerance=±5% resistance=220 package=THT]
  S1 = Pushbutton [package="[SMD]"]
  S2 = Pushbutton [package="[SMD]"]
  J1 = Camdenboss CTB0158-2 [part_number=CTB0158-2 package=THT]

nets:
  N1: NodeMCU.D1, M1.A
  N2: NodeMCU.D2, M1.C
  N3: NodeMCU.D3, M1.B
  N4: NodeMCU.D4, M1.D
  N5: NodeMCU.GND, LED1.cathode, LED0.cathode, J1.pin2
  N6: NodeMCU.D5, S2.Pin_1, S2.Pin_2
  N7: NodeMCU.D6, S1.Pin_1, S1.Pin_2
  N8: NodeMCU.D7, R2.Pin_1
  N9: NodeMCU.D8, R1.Pin_0
  N10: NodeMCU.Vin, J1.pin1
  N11: LED1.anode, R1.Pin_1
  N12: LED0.anode, R2.Pin_0
  N13: S1.Pin_3, S1.Pin_4
  N14: S2.Pin_3, S2.Pin_4

custom parts:
  ESP8266 NodeMCU LoLin module: ESP8266 based NodeMCU
