# Fritzing sketch ESP8266_PCB_female (saved by Fritzing 0.9.4)
perfboards: 1

parts:
  J2 = female pin header, 14 pins [form="♀ (female)"]  # not connected
  J3 = screw terminal, 12 pins  # not connected
  J4 = screw terminal, 12 pins  # not connected
  VCC1 = Battery  # not connected
  U1 = NodeMCU V3.0  # not connected
  J1 = female pin header, 15 pins [form="♀ (female)"]
  RTC_(DS3231) = ZS-042 RTC Module
  KY-1 = Keyes Relay [package=THT]  # not connected
  Depo_Vacío = LED - 5mm [color="Red (633nm)" package="5 mm [THT]"]  # not connected
  Regando = LED - 5mm [color="Green (555nm)" package="5 mm [THT]"]  # not connected
  OTA/START = LED - 5mm [color="Blue (470nm)" package="5 mm [THT]"]  # not connected
  LED1 = LEDs [package=led10mm]  # not connected

nets:
  N1: J1.pin2, RTC_(DS3231).SDA
  N2: J1.pin3, RTC_(DS3231).VCC

custom parts:
  NodeMCU V3.0: ESP8266 based NodeMCU
  Keyes Relay: The Keyes 5V relay module is suitable for SCM development, home appliance control. It uses a 5V~12V TIL control signal which can control DC / AC signal.
